// Logisim project Mux21c.circ as structural Verilog: 1 circuit, main circuit main
module main (
  input  i0,
  input  i1,
  input  S,
  output out_4,
  output out_5,
  output out_6
);

  wire nand_1_out, nand_2_out, nand_3_out;

  nand nand_1 (nand_1_out, i1, S);
  nand nand_2 (nand_2_out, S, S);
  Multiplexer multiplexer_1 (.in0(i0), .in1(i1), .out(out_6), .sel(S));  // open: en
  nand nand_3 (nand_3_out, i0, nand_2_out);
  nand nand_4 (out_4, nand_1_out, nand_3_out);
  xnor xnor_1 (out_5, out_4, out_6);

  // Notes on the sheet:
  //   Test Mux for correct input
  //   Output of the Nand gates
endmodule
